# Fritzing sketch TaichiArduboy (saved by Fritzing 0.9.3b)
breadboards: 1

parts:
  S1 = Pushbutton [package="[THT]"]
  S2 = Pushbutton [package="[THT]"]
  SPI_SSD1 = OLED 0.96" 128x64 SPI SSD1306
  Pro_Micro1 = Pro Micro  # not connected
  S3 = Pushbutton [package="[THT]"]
  S4 = Pushbutton [package="[THT]"]
  S5 = Pushbutton [package="[THT]"]
  S6 = Pushbutton [package="[THT]"]
  YwRobot_Power_Supply1 = YwRobot Breadboard Power Supply [part_number=545043]
  J1 = Piezo Speaker

nets:
  N1: S1.Pin_1, S1.Pin_2, YwRobot_Power_Supply1.GND#13, YwRobot_Power_Supply1.GND#14
  N2: S1.Pin_3, S1.Pin_4
  N3: S2.Pin_1, S2.Pin_2, SPI_SSD1.GND, SPI_SSD1.CS, S3.Pin_1, S3.Pin_2, S4.Pin_3, S4.Pin_4, YwRobot_Power_Supply1.GND#11, YwRobot_Power_Supply1.GND#12, J1.pin1
  N4: S2.Pin_3, S2.Pin_4
  N5: SPI_SSD1.VCC, YwRobot_Power_Supply1.VCC#5, YwRobot_Power_Supply1.VCC#6
  N6: S3.Pin_3, S3.Pin_4
  N7: S4.Pin_1, S4.Pin_2
  N8: S5.Pin_1, S5.Pin_2
  N9: S5.Pin_3, S5.Pin_4
  N10: S6.Pin_1, S6.Pin_2
  N11: S6.Pin_3, S6.Pin_4
  N12: YwRobot_Power_Supply1.VCC#9, YwRobot_Power_Supply1.VCC#10

custom parts:
  Pro Micro: The SparkFun Pro Micro is a complete USB-based microcontoller development system, in a very small footprint, capable of implementing many types of projects. All programming can be done via the USB port.
  YwRobot Breadboard Power Supply: The YwRobot Breadboard Power Supply (MB-V2) has two power rails; they can be 5V or 3V3. Power to the module can be provided through the female USB socket or through the A10 (female) 2.1mm power jack.
