# Fritzing sketch pong_hardware (saved by Fritzing 0.9.3b)
breadboards: 1

parts:
  U1 = NodeMCU V1.0
  o1 = Module display OLED I2C 128x64 SSD1306 [package=THT]
  S1 = Pushbutton [package="[THT]"]
  S2 = Pushbutton [package="[THT]"]

nets:
  N1: U1.D1, o1.SCL
  N2: U1.D2, o1.SDA
  3V3: U1.3V3, o1.VCC
  GND: U1.GND, o1.GND, S1.Pin_1, S1.Pin_2, S2.Pin_3, S2.Pin_4
  N3: U1.D5, S1.Pin_3, S1.Pin_4
  N4: U1.D6, S2.Pin_1, S2.Pin_2

custom parts:
  NodeMCU V1.0: ESP8266 based NodeMCU
  Module display OLED I2C 128x64 SSD1306: Ecran OLED I2C SSD163 de 128x64 avec connexion I2C
